# Fritzing sketch mainboard (saved by Fritzing 0.9.3b)
circuit board: 6.90647cm x 4.83314cm
breadboards: 1

parts:
  IC1 = L293D [package=THT]
  RIGHT = DC Motor
  LEFT = DC Motor
  Q1 = NPN-Transistor [package="TO92 [THT]"]
  R1 = Resistor [tolerance=±5% resistance=220 package=THT]
  Q2 = NPN-Transistor [package="TO92 [THT]"]
  R2 = Resistor [tolerance=±5% resistance=1k package=THT]
  hc-sr1 = hc-sr04
  hc-sr2 = hc-sr04
  hc-sr3 = hc-sr04
  RELAY = RELAY [package=relay-jzc]
  Q4 = NPN-Transistor [package="TO92 [THT]"]
  R3 = Resistor [tolerance=±5% resistance=220 package=THT]
  LED1 = LED - 5mm [color="Green (555nm)" package="5 mm [THT]"]
  R4 = Resistor [tolerance=±5% resistance=220 package=THT]
  D1 = Schottky Diode [part_number=1N5817 package="300 mil [THT]"]
  D2 = Schottky Diode [part_number=1N5817 breakdown_voltage=3.6V package="300 mil [THT]"]
  VAC = DC Motor
  Raspberry_Pi_1 = Raspberry Pi 3 [part_number=RPI-3-V1.2]
  ON = Power plug
  VCC1 = Battery
  D3 = Schottky Diode [part_number=1N5817 package="300 mil [THT]"]
  CHRG = female pin header, 2 pins [form="♀ (female)"]
  OFF = Toggle Switch [package=THT]
  R5 = Resistor [tolerance=±5% resistance=220 package=THT]
  R6 = Resistor [tolerance=±5% resistance=220 package=THT]
  Speaker = Piezo Speaker
  Q3 = NPN-Transistor [package="TO92 [THT]"]

nets:
  N1: IC1.Enable_1, IC1.Enable_2, Raspberry_Pi_1.GIPO13
  N2: IC1.In_1, R1.Pin_0, Raspberry_Pi_1.GIPO5
  N3: IC1.Out_1_(_Controlled_by_Enable_1_), LEFT.pin_1
  GND: IC1.0V, Q1.E, Q2.E, hc-sr1.GND, hc-sr2.GND, hc-sr3.GND, Q4.E, LED1.cathode, VAC.pin_1, Raspberry_Pi_1.GND, ON.GND, VCC1.-, CHRG.pin1, Q3.E
  N4: IC1.Out_2_(_Controlled_by_Enable_1_), LEFT.pin_2
  N5: IC1.In_2, Q1.C, R5.Pin_1
  VCC: IC1.+Vmotor, hc-sr1.VCC, hc-sr2.VCC, hc-sr3.VCC, RELAY.NC, RELAY.COIL1, D1.anode, D2.cathode, OFF.COM, Speaker.pin2
  N6: IC1.In_3, Q2.C, R6.Pin_1
  N7: IC1.Out_3_(_Controlled_by_Enable_2_), RIGHT.pin_2
  N8: IC1.Out_4_(_Controlled_by_Enable_2_), RIGHT.pin_1
  N9: IC1.In_4, R2.Pin_0, Raspberry_Pi_1.GIPO6
  3V3: IC1.+V, Raspberry_Pi_1.3v3, Raspberry_Pi_1.3V3, R5.Pin_0, R6.Pin_0
  N10: Q1.B, R1.Pin_1
  N11: Q2.B, R2.Pin_1
  N12: hc-sr1.Trig, Raspberry_Pi_1.GIPO12
  N13: hc-sr1.Echo, Raspberry_Pi_1.GIPO16
  N14: hc-sr2.Trig, Raspberry_Pi_1.GIPO20
  N15: hc-sr2.Echo, Raspberry_Pi_1.GIPO21
  N16: hc-sr3.Trig, Raspberry_Pi_1.GIPO19
  N17: hc-sr3.Echo, Raspberry_Pi_1.GIPO26
  N18: RELAY.COIL2, Q4.C, D2.anode
  N19: RELAY.MAIN, VAC.pin_2
  N20: Q4.B, R3.Pin_1
  N21: R3.Pin_0, Raspberry_Pi_1.GIPO4
  N22: LED1.anode, R4.Pin_1
  N23: R4.Pin_0, Raspberry_Pi_1.GIPO17
  N24: D1.cathode, Raspberry_Pi_1.5V
  N25: Raspberry_Pi_1.GIPO27, Q3.B
  N26: ON.VCC, D3.cathode, OFF.L2
  N27: VCC1.+, D3.anode, CHRG.pin2
  N28: Speaker.pin1, Q3.C

notes:
  Spot V.2
